# Fritzing sketch GameConsole_V1.2.2 (saved by Fritzing 0.9.4)
breadboards: 1

parts:
  Part1 = Arduino Uno (Rev3)
  Part2 = Thumb Joystick
  Part3 = Thumb Joystick
  Part4 = LED Matrix - Serial Interface - Red/Green/Blue
  Part5 = LED Matrix - Serial Interface - Red/Green/Blue
  Part6 = LED Matrix - Serial Interface - Red/Green/Blue
  Part7 = LED Matrix - Serial Interface - Red/Green/Blue

nets:
  N1: Part1.A0, Part2.VERT
  N2: Part1.A1, Part2.HORZ
  N3: Part1.A2, Part2.SEL
  N4: Part1.A3, Part3.VERT
  N5: Part1.A4/SDA, Part3.HORZ
  GND: Part1.A5/SCL, Part1.GND, Part2.GND, Part3.GND, Part3.SEL, Part4.GND, Part5.GND, Part6.GND, Part7.GND
  N6: Part1.D10_PWM/SS, Part4.SCK, Part5.SCK, Part6.SCK, Part7.SCK
  N7: Part1.D11_PWM/MOSI, Part4.CS, Part5.CS, Part6.CS, Part7.CS
  N8: Part1.D12/MISO, Part4.MISO
  VCC: Part1.5V, Part2.VCC, Part3.VCC, Part4.VCC, Part5.VCC, Part6.VCC, Part7.VCC
  N9: Part4.MOSI, Part5.MISO
  N10: Part5.MOSI, Part6.MISO
  N11: Part6.MOSI, Part7.MISO
